# Fritzing sketch tervezet (saved by Fritzing 0.9.10b)
breadboards: 2

parts:
  Part1 = Arduino Nano (Rev3.0)
  LED_Matrix_8x8 = 38mm 8x8 dot matrix row cathode led display with standard pcb pads
  Driver1 = 28BYJ-48 Driver Module [part_number=ULN2003 package=THT]
  SM1 = 28BYJ-48 Stepper Motor [part_number=28BYJ-48]
  Part3 = Arduino Nano (Rev3.0)
  R1 = Resistor [tolerance=±5% resistance=10k package="1206 [SMD]"]
  R2 = Resistor [tolerance=±5% resistance=10k package="1206 [SMD]"]
  R3 = Resistor [tolerance=±5% resistance=10k package="1206 [SMD]"]
  R4 = Resistor [tolerance=±5% resistance=10k package="1206 [SMD]"]
  R5 = Resistor [tolerance=±5% resistance=10k package="1206 [SMD]"]
  R6 = Resistor [tolerance=±5% resistance=10k package="1206 [SMD]"]
  R7 = Resistor [tolerance=±5% resistance=10k package="1206 [SMD]"]
  HC-SR04_Sensor_1 = HC-SR04 Ultrasonic Distance Sensor
  R8 = Resistor [tolerance=±5% resistance=10k package="1206 [SMD]"]
  Buzzer = Piezo Speaker
  VCC1 = Battery

nets:
  N1: Part1.D1/TX, Part3.D0/RX
  N2: Part1.D0/RX, Part3.D1/TX
  GND: Part1.GND, Part3.GND, HC-SR04_Sensor_1.GND, Buzzer.pin1
  N3: Part1.D6, Driver1.IN1
  N4: Part1.D7, Driver1.IN2
  N5: Part1.D8, Driver1.IN3
  N6: Part1.D9, Driver1.IN4
  N7: Part1.D10, HC-SR04_Sensor_1.ECHO
  N8: Part1.D11/MOSI, HC-SR04_Sensor_1.TRIG
  N9: Part1.D12/MISO, Buzzer.pin2
  VIN: Part1.VIN, Part3.VIN
  5V: Part1.5V, HC-SR04_Sensor_1.VCC
  N10: LED_Matrix_8x8.pin_1, R5.Pin_0
  N11: LED_Matrix_8x8.pin_2, R7.Pin_0
  N12: LED_Matrix_8x8.pin_3, Part3.D11/MOSI
  N13: LED_Matrix_8x8.pin_4, Part3.D12/MISO
  N14: LED_Matrix_8x8.pin_5, R8.Pin_0
  N15: LED_Matrix_8x8.pin_6, Part3.A0
  N16: LED_Matrix_8x8.pin_7, R6.Pin_0
  N17: LED_Matrix_8x8.pin_8, R3.Pin_0
  N18: LED_Matrix_8x8.pin_9, R1.Pin_0
  N19: LED_Matrix_8x8.pin_10, Part3.D13/SCK
  N20: LED_Matrix_8x8.pin_11, Part3.A1
  N21: LED_Matrix_8x8.pin_12, R2.Pin_0
  N22: LED_Matrix_8x8.pin_13, Part3.D10
  N23: LED_Matrix_8x8.pin_14, R4.Pin_0
  N24: LED_Matrix_8x8.pin_15, Part3.A2
  N25: LED_Matrix_8x8.pin_16, Part3.A3
  N26: Driver1.GND, VCC1.-
  N27: Driver1.Vmotor, VCC1.+
  N28: Driver1.blue-pin, SM1.blue-pin
  N29: Driver1.pink-pin, SM1.pink-pin
  N30: Driver1.yellow-pin, SM1.yellow-pin
  N31: Driver1.orange-pin, SM1.orange-pin
  N32: Driver1.red-pin, SM1.red-pin
  N33: Part3.D2, R1.Pin_1
  N34: Part3.D3, R4.Pin_1
  N35: Part3.D4, R3.Pin_1
  N36: Part3.D5, R2.Pin_1
  N37: Part3.D6, R5.Pin_1
  N38: Part3.D7, R6.Pin_1
  N39: Part3.D8, R7.Pin_1
  N40: Part3.D9, R8.Pin_1

custom parts:
  28BYJ-48 Driver Module: ULN2003 Driver Module for the 28BYJ-48 Unipolar Stepper Motor LED A - Blue wire - Bottom coil left LED B - Pink wire - Top coil left LED C - Yellow wire - Bottom coil right LED D - Orange wire - Top coil right Common rail - red Connector pins: blue - pink - yellow - orange - red Control pins - IN1 to IN4 Power pins - GND & Vmotor (5-12V) On/Off jumper (if removed, power to motor is cut).
  28BYJ-48 Stepper Motor: Unipolar Stepper Motor 28BYJ-48 Top coil - pink & orange Bottom coil - blue & yellow Common rail - red Connector pins: blue - pink - yellow - orange - red
